# Fritzing sketch stalker (saved by Fritzing 0.8.7b)
breadboards: 1

parts:
  R1 = Resistor [tolerance=±5% resistance=22k package=THT]
  U1 = atmega328 [package=dip]
  Y1 = CRYSTAL [package=crystal-smd-10.5x4.8-2pin]
  C2 = Ceramic Capacitor [capacitance=22µF package="100 mil [THT, multilayer]"]
  C3 = Ceramic Capacitor [capacitance=22µF package="100 mil [THT, multilayer]"]
  C4 = Ceramic Capacitor [capacitance=22µF package="100 mil [THT, multilayer]"]
  U2 = Battery Holders [package=lipo-1100mAh]
  U3 = TEMPERATURE-SENSOR [package=to-92]
  Part1 = Real Time Clock Module - DS1307 RTC Breakout Board

nets:
  N1: R1.Pin_0, U1.RESET
  N2: R1.Pin_1, U1.VCC, U1.AVCC, C4.1, U2.+
  N3: U1.GND, C2.1, C3.1, C4.0
  N4: U1.XLAT1, Y1.1, C3.0
  N5: U1.XLAT2, Y1.2, C2.0
  N6: U1.D8, U3.VCC
  N7: U1.D9_(PWM), Part1.5V
  N8: U1.A0, U3.ADJ
  N9: U1.A4, Part1.SDA
  N10: U1.A5, Part1.SCL
  GND: U2.-, U3.GND, Part1.GND

notes:
  Real Time Clock + 32kB EEPROM
  Hall Sensor
